// Logisim project Project1.circ as structural Verilog: 10 circuits, main circuit main
module main (
);

  wire Clock, d_ff_1_q, JumpSig, Noop1, Noop2, Reset, Stall, StallClock, WrSig;
  wire [3:0] ExReg, id_rr_1_destreg, if_1_rd, if_1_rs, if_1_rt, MemReg, Rd_q, Rs_q, Rt_q, WrReg;
  wire [8:0] if_1_opcode, Opcode_2_q, Opcode_3_q, Opcode_4_q, Opcode_q;
  wire [15:0] if_1_imm, Imm_q;
  wire [31:0] Data1_q, Data2_q, ex_1_out, ex_1_swrt, id_rr_1_data1, id_rr_1_data2, id_rr_1_extimm, Imm_2_q,
       IncPC_2_q, IncPC_q, JumpPc, Out_2_q, Out_q, SwRt_q, undriven, undriven_2, WrRegData;

  Clock u_Clock (.out(Clock));
  Button u_Reset (.out(Reset));
  IF if_1 (
    .Clock(StallClock), .Reset(Reset), .JumpPC(JumpPc), .JumpSig(JumpSig), .PC_4(undriven), .Rs(if_1_rs),
    .Rt(if_1_rt), .Rd(if_1_rd), .Imm(if_1_imm), .Opcode(if_1_opcode));
  Register #(.width(32)) IncPC (.D(undriven), .Q(IncPC_q), .clk(StallClock), .clr(JumpSig));  // open: en
  Register #(.width(4)) Rs (.D(if_1_rs), .Q(Rs_q), .clk(StallClock), .clr(JumpSig));  // open: en
  Register #(.width(4)) Rt (.D(if_1_rt), .Q(Rt_q), .clk(StallClock), .clr(JumpSig));  // open: en
  Register #(.width(4)) Rd (.D(if_1_rd), .Q(Rd_q), .clk(StallClock), .clr(JumpSig));  // open: en
  Register #(.width(16)) Imm (.D(if_1_imm), .Q(Imm_q), .clk(StallClock), .clr(JumpSig));  // open: en
  Register #(.width(9)) Opcode (.D(if_1_opcode), .Q(Opcode_q), .clk(StallClock), .clr(JumpSig));  // open: en
  or or_1 (JumpSig, Reset, Noop1);
  or or_2 (Stall, Noop2, Noop1);
  or or_3 (JumpSig, Reset, Noop2);
  ID_RR id_rr_1 (
    .Rs(Rs_q), .Rt(Rt_q), .Rd(Rd_q), .Imm(Imm_q), .Opcode(Opcode_q), .WrSig(WrSig), .WrRegData(WrRegData),
    .WrReg(WrReg), .MemReg(MemReg), .ExReg(ExReg), .Noop2(Noop2), .Clock(Clock), .Noop1(Noop1),
    .Data1(id_rr_1_data1), .Data2(id_rr_1_data2), .ExtImm(id_rr_1_extimm), .DestReg(id_rr_1_destreg));
  Register #(.width(32)) IncPC_2 (.D(IncPC_q), .Q(IncPC_2_q), .clk(Clock), .clr(JumpSig));  // open: en
  Register #(.width(32)) Data1 (.D(id_rr_1_data1), .Q(Data1_q), .clk(Clock), .clr(JumpSig));  // open: en
  Register #(.width(32)) Data2 (.D(id_rr_1_data2), .Q(Data2_q), .clk(Clock), .clr(JumpSig));  // open: en
  Register #(.width(32)) Imm_2 (.D(id_rr_1_extimm), .Q(Imm_2_q), .clk(Clock), .clr(JumpSig));  // open: en
  Register #(.width(4)) DestReg (.D(id_rr_1_destreg), .Q(ExReg), .clk(Clock), .clr(JumpSig));  // open: en
  Register #(.width(9)) Opcode_2 (.D(Opcode_q), .Q(Opcode_2_q), .clk(Clock), .clr(JumpSig));  // open: en
  Ex ex_1 (
    .PC_4(IncPC_2_q), .Data1(Data1_q), .Data2(Data2_q), .Imm(Imm_2_q), .Opcode(Opcode_2_q), .JumpPC(JumpPc),
    .Out(ex_1_out), .SwRt(ex_1_swrt), .JumpSig(JumpSig));
  Register #(.width(32)) Out (.D(ex_1_out), .Q(Out_q), .clk(Clock), .clr(Reset));  // open: en
  Register #(.width(32)) SwRt (.D(ex_1_swrt), .Q(SwRt_q), .clk(Clock), .clr(Reset));  // open: en
  Register #(.width(4)) DestReg_2 (.D(ExReg), .Q(MemReg), .clk(Clock), .clr(Reset));  // open: en
  Register #(.width(9)) Opcode_3 (.D(Opcode_2_q), .Q(Opcode_3_q), .clk(Clock), .clr(Reset));  // open: en
  Multiplexer #(.enable("false")) multiplexer_1 (.in0(Clock), .in1(1'b0), .out(StallClock), .sel(d_ff_1_q));
  D_Flip_Flop d_ff_1 (.clk(Clock), .D(Stall), .Q(d_ff_1_q));  // open: Qn, preset, en, reset
  Mem mem_1 (.Rs_Imm(Out_q), .SwRt(SwRt_q), .Opcode(Opcode_3_q), .Clock(Clock), .Out(undriven_2));
  Register #(.width(32)) Out_2 (.D(undriven_2), .Q(Out_2_q), .clk(Clock), .clr(Reset));  // open: en
  Register #(.width(4)) DestReg_3 (.D(MemReg), .Q(WrReg), .clk(Clock), .clr(Reset));  // open: en
  Register #(.width(9)) Opcode_4 (.D(Opcode_3_q), .Q(Opcode_4_q), .clk(Clock), .clr(Reset));  // open: en
  WB wb_1 (.LW_Out(Out_2_q), .Opcode(Opcode_4_q), .WrRegData(WrRegData), .WrSig(WrSig));

  // Other names for the same wires on the sheet: Res_Noop1 = JumpSig; Res_Noop2 = JumpSig
endmodule

module IF (
  input  JumpSig,
  input  Clock,
  input  Reset,
  input  [31:0] JumpPC,
  input  [31:0] PC_4,
  output [3:0] Rs,
  output [3:0] Rt,
  output [3:0] Rd,
  output [15:0] Imm,
  output [8:0] Opcode
);

  wire [7:0] bit_extender_2_out;
  wire [10:0] bit_extender_1_out;
  wire [31:0] multiplexer_1_out, multiplexer_2_out, PC_q;
  wire [31:24] Imem_data;

  Multiplexer #(.width(32), .enable("false")) multiplexer_1 (
    .in0(multiplexer_2_out), .in1(32'h100), .out(multiplexer_1_out), .sel(Reset));
  Multiplexer #(.width(32), .enable("false")) multiplexer_2 (
    .in0(PC_4), .in1(JumpPC), .out(multiplexer_2_out), .sel(JumpSig));
  Register #(.width(32)) PC (.D(multiplexer_1_out), .Q(PC_q), .clk(Clock));  // open: en, clr
  Bit_Extender #(.in_width(32), .out_width(11)) bit_extender_1 (.in(PC_q), .out(bit_extender_1_out));
  memory Imem (.A(bit_extender_1_out), .Clock(Clock), .Data({Imem_data, Imm, Rs, Rt}));  // open: en, Load, Clear
  Comparator #(.width(6)) comparator_1 (.a({6{1'b0}}), .b(Imem_data[31:26]), .eq(Opcode[8]));  // open: gt, lt
  assign bit_extender_2_out = {{2{1'b0}}, Imem_data[31:26]};  // Bit_Extender bit_extender_2
  Multiplexer #(.width(8), .enable("false")) multiplexer_3 (
    .in0(bit_extender_2_out), .in1({Imem_data[25:24], Imm[15:10]}), .out(Opcode[7:0]), .sel(Opcode[8]));
  Adder #(.width(32)) adder_1 (.a(32'h4), .b(PC_q), .out(PC_4));  // open: cin, cout

  assign Rd = Imm[3:0];
endmodule

module memory (
  input  [10:0] A,
  input  en,
  input  Clock,
  input  Load,
  input  Clear,
  output [31:0] Data
);

  RAM #(.addrWidth(11), .dataWidth(32)) ram_1 (.addr(A), .data(Data), .sel(en), .clk(Clock), .ld(Load), .clr(Clear));

  // Notes on the sheet:
  //   Shoud be byte addressable memory. In other words, 13 bits for address memory of 1 byte each, but gives 32 bits (4 bytes) of mem.
endmodule

module ID_RR (
  input  WrSig,
  input  [3:0] WrReg,
  input  [3:0] MemReg,
  input  [3:0] ExReg,
  input  [31:0] WrRegData,
  input  [3:0] Rs,
  input  [3:0] Rt,
  input  [3:0] Rd,
  input  [15:0] Imm,
  input  [8:0] Opcode,
  input  Clock,
  output [31:0] Data1,
  output [31:0] Data2,
  output [31:0] ExtImm,
  output [3:0] DestReg,
  output Noop2,
  output Noop1
);

  wire and_1_out, and_2_out, comparator_1_eq, comparator_2_eq, comparator_3_eq, comparator_4_eq,
       comparator_5_eq, comparator_6_eq, comparator_7_eq, comparator_8_eq, comparator_9_eq, not_1_out,
       not_2_out, or_1_out, or_2_out, or_4_out, signalgen_1_beq, signalgen_1_ble, signalgen_1_blt,
       signalgen_1_bneq, signalgen_1_sw;
  wire [3:0] DestReg_t;

  assign ExtImm = {{16{Imm[15]}}, Imm};  // Bit_Extender bit_extender_1
  Multiplexer #(.width(4), .disabled(0), .enable("false")) multiplexer_1 (
    .in0(Rt), .in1(Rd), .out(DestReg_t), .sel(Opcode[8]));
  Comparator #(.width(4)) comparator_1 (.a(Rs), .b(WrReg), .eq(comparator_1_eq));  // open: gt, lt
  Comparator #(.width(4)) comparator_2 (.a(Rs), .b(MemReg), .eq(comparator_2_eq));  // open: gt, lt
  Comparator #(.width(4)) comparator_3 (.a(Rs), .b(ExReg), .eq(comparator_3_eq));  // open: gt, lt
  Comparator #(.width(4)) comparator_4 (.a(Rs), .b(4'b0000), .eq(comparator_4_eq));  // open: gt, lt
  Comparator #(.width(4)) comparator_5 (.a(DestReg_t), .b(WrReg), .eq(comparator_5_eq));  // open: gt, lt
  Comparator #(.width(4)) comparator_6 (.a(DestReg_t), .b(MemReg), .eq(comparator_6_eq));  // open: gt, lt
  Comparator #(.width(4)) comparator_7 (.a(DestReg_t), .b(ExReg), .eq(comparator_7_eq));  // open: gt, lt
  Comparator #(.width(4)) comparator_8 (.a(DestReg_t), .b(4'b0000), .eq(comparator_8_eq));  // open: gt, lt
  not not_1 (not_1_out, comparator_8_eq);
  or or_1 (or_1_out, comparator_1_eq, comparator_2_eq, comparator_3_eq);
  not not_2 (not_2_out, comparator_4_eq);
  or or_2 (or_2_out, comparator_5_eq, comparator_6_eq, comparator_7_eq);
  and and_1 (and_1_out, or_2_out, not_1_out);
  and and_2 (and_2_out, or_1_out, not_2_out);
  DPRF dprf_1 (
    .Clock(Clock), .RdSrc1(Rs), .RdSrc2(Rt), .RdData1(Data1), .RdData2(Data2), .WrDest(WrReg),
    .WrData(WrRegData), .WrEn(WrSig));
  or or_3 (Noop2, and_2_out, and_1_out);
  SignalGen signalgen_1 (
    .Opcode(Opcode), .Beq(signalgen_1_beq), .Blt(signalgen_1_blt), .Ble(signalgen_1_ble),
    .Bneq(signalgen_1_bneq), .Sw(signalgen_1_sw));  // open: Eq, Lt, Le, Neq, Add, And, Or, Xor, Sub, Nand, Nor, Nxor, Rshf, Lshf, Jal, Lw, Addi, Andi, Ori, Xori
  Multiplexer #(.width(4), .enable("false")) multiplexer_2 (
    .in0(DestReg_t), .in1(4'b0000), .out(DestReg), .sel(or_4_out));
  or or_4 (or_4_out, signalgen_1_beq, signalgen_1_blt, signalgen_1_ble, signalgen_1_bneq, signalgen_1_sw);
  Comparator #(.width(4)) comparator_9 (.a(Opcode[5:2]), .b(4'b0010), .eq(comparator_9_eq));  // open: gt, lt
  and and_3 (Noop1, Opcode[8], comparator_9_eq);

  // Other names for the same wires on the sheet: Op[7:0] = Opcode[7:0]; Ext = Opcode[8]
endmodule

module Ex (
  input  [31:0] PC_4,
  input  [31:0] Data1,
  input  [31:0] Data2,
  input  [31:0] Imm,
  input  [8:0] Opcode,
  output [31:0] JumpPC,
  output [31:0] Out,
  output [31:0] SwRt,
  output JumpSig
);

  wire Add, Addi, Alu, And, and_1_out, and_2_out, and_3_out, and_4_out, and_5_out, and_6_out, and_7_out,
       and_8_out, and_9_out, and_10_out, and_11_out, Andi, B_Eq, B_Le, B_Lt, B_Neq, Beq, Ble, Blt, Bneq,
       Bran, comparator_1_eq, comparator_2_eq, comparator_2_gt, comparator_2_lt, comparator_3_eq,
       demultiplexer_1_out0, Eq, Ext1, JBran, Le, Lshf, Lt, Lw, Nand, Neq, Nor, Nxor, Or, or_9_out, Ori,
       Rshf, Sub, Sw, Xor, Xori;
  wire [2:0] Func;
  wire [4:0] bit_extender_1_out, bit_extender_2_out;
  wire [31:0] _4xImm, adder_1_out, alu_1_out, bit_extender_3_out, multiplexer_1_out, multiplexer_2_out,
       shifter_2_out, shifter_3_out;

  or or_1 (Bran, Ble, Bneq, Beq, Blt);
  or or_2 (B_Le, Le, Ble);
  or or_3 (B_Neq, Neq, Bneq);
  or or_4 (B_Eq, Eq, Beq);
  or or_5 (B_Lt, Lt, Blt);
  or or_6 (JBran, Bran, JumpSig);
  Comparator #(.width(2)) comparator_1 (.a(Opcode[5:4]), .b(2'b10), .eq(comparator_1_eq));  // open: gt, lt
  Multiplexer #(.width(32), .enable("false")) multiplexer_1 (
    .in0(Imm), .in1(Data2), .out(multiplexer_1_out), .sel(Opcode[8]));
  Shifter #(.width(32)) shifter_1 (.in(Imm), .\dist (5'b00010), .out(_4xImm));
  Shifter #(.width(32)) shifter_2 (.in(Data1), .\dist (bit_extender_1_out), .out(shifter_2_out));
  Bit_Extender #(.in_width(32), .out_width(5), .\type ("sign")) bit_extender_1 (.in(Data2), .out(bit_extender_1_out));
  Comparator #(.width(32)) comparator_2 (
    .a(Data1), .b(Data2), .gt(comparator_2_gt), .eq(comparator_2_eq), .lt(comparator_2_lt));
  or or_7 (Alu, comparator_1_eq, comparator_3_eq);
  Comparator #(.width(3)) comparator_3 (
    .a({Opcode[8], Opcode[5:4]}), .b(3'b101), .eq(comparator_3_eq));  // open: gt, lt
  ALU alu_1 (.A(Data1), .B(multiplexer_1_out), .Func(Func), .Out(alu_1_out));
  assign Out = Alu ? alu_1_out : 32'bz;  // Controlled_Buffer controlled_buffer_1
  assign Out = Lshf ? shifter_2_out : 32'bz;  // Controlled_Buffer controlled_buffer_2
  and and_1 (and_1_out, B_Le, ~comparator_2_gt);  // AND_Gate
  and and_2 (and_2_out, comparator_2_lt, B_Lt);
  and and_3 (and_3_out, ~Opcode[0], ~Opcode[1], Opcode[2], ~Opcode[3]);  // AND_Gate
  and and_4 (and_4_out, B_Neq, ~comparator_2_eq);  // AND_Gate
  and and_5 (and_5_out, comparator_2_eq, B_Eq);
  or or_8 (Func[2], and_3_out, and_6_out, and_9_out, and_11_out);
  and and_6 (and_6_out, ~Opcode[0], Opcode[1], Opcode[2], ~Opcode[3]);  // AND_Gate
  and and_7 (and_7_out, Opcode[0], ~Opcode[1], Opcode[2], ~Opcode[3]);  // AND_Gate
  or or_9 (or_9_out, and_1_out, and_4_out, and_5_out, and_2_out);
  or or_10 (Func[0], and_8_out, and_9_out, and_10_out, and_11_out);
  or or_11 (Func[1], and_7_out, and_6_out, and_10_out, and_11_out);
  and and_8 (and_8_out, ~Opcode[0], ~Opcode[1], ~Opcode[2], Opcode[3]);  // AND_Gate
  Multiplexer #(.width(32), .enable("false")) multiplexer_2 (
    .in0(Data1), .in1(PC_4), .out(multiplexer_2_out), .sel(Bran));
  Shifter #(.width(32), .shift("ar")) shifter_3 (.in(Data1), .\dist (bit_extender_2_out), .out(shifter_3_out));
  Bit_Extender #(.in_width(32), .out_width(5), .\type ("sign")) bit_extender_2 (.in(Data2), .out(bit_extender_2_out));
  Demultiplexer #(.enable("false")) demultiplexer_1 (
    .out0(demultiplexer_1_out0), .out1(JumpSig), .in(or_9_out), .sel(Bran));
  and and_9 (and_9_out, ~Opcode[0], ~Opcode[1], Opcode[2], Opcode[3]);  // AND_Gate
  Adder #(.width(32)) adder_1 (.a(multiplexer_2_out), .b(_4xImm), .out(adder_1_out));  // open: cin, cout
  assign Out = Rshf ? shifter_3_out : 32'bz;  // Controlled_Buffer controlled_buffer_3
  assign bit_extender_3_out = {{31{1'b0}}, demultiplexer_1_out0};  // Bit_Extender bit_extender_3
  assign Out = Ext1 ? bit_extender_3_out : 32'bz;  // Controlled_Buffer controlled_buffer_4
  and and_10 (and_10_out, Opcode[0], ~Opcode[1], Opcode[2], Opcode[3]);  // AND_Gate
  and and_11 (and_11_out, ~Opcode[0], Opcode[1], Opcode[2], Opcode[3]);  // AND_Gate
  assign JumpPC = JumpSig ? adder_1_out : 32'bz;  // Controlled_Buffer controlled_buffer_5
  SignalGen signalgen_1 (
    .Opcode(Opcode), .Eq(Eq), .Lt(Lt), .Le(Le), .Neq(Neq), .Add(Add), .And(And), .Or(Or), .Xor(Xor),
    .Sub(Sub), .Nand(Nand), .Nor(Nor), .Nxor(Nxor), .Rshf(Rshf), .Lshf(Lshf), .Beq(Beq), .Blt(Blt),
    .Ble(Ble), .Bneq(Bneq), .Jal(JumpSig), .Lw(Lw), .Sw(Sw), .Addi(Addi), .Andi(Andi), .Ori(Ori), .Xori(Xori));
  assign SwRt = Sw ? Data2 : 32'bz;  // Controlled_Buffer controlled_buffer_6
  assign Out = JumpSig ? PC_4 : 32'bz;  // Controlled_Buffer controlled_buffer_7

  // Other names for the same wires on the sheet: Jal = JumpSig; Op[7:0] = Opcode[7:0]; Ext = Opcode[8]

  // Notes on the sheet:
  //   ALU Functions
  //   (L/S)W Fucntion
  //   sext(imm) * 4
  //   Replace in Verilog with wire
  //   Regular ALU functions
  //   Replace in Verilog with wire
  //   Left shift function
  //   These are all non-add instructions. State defaults to add (which is good because L/S word uses add)
  //   Replace in Verilog with wire
  //   Comparison circuit (for ALU compare and branch decisions)
  //   Right shift function (arithmetic)
  //   JumpSig: JAL + out from comparison circuit
endmodule

module Mem (
  input  [31:0] Rs_Imm,
  input  [31:0] SwRt,
  input  [31:0] Out,
  input  [8:0] Opcode,
  input  Clock
);

  wire Lw, not_1_out, Sw;
  wire [10:0] bit_extender_1_out;
  wire [31:0] controlled_buffer_2_out, dmem_data;

  and and_1 (Sw, Opcode[3], Opcode[4], ~Opcode[5], Opcode[8]);  // AND_Gate
  and and_2 (Lw, ~Opcode[3], Opcode[4], ~Opcode[5], Opcode[8]);  // AND_Gate
  Bit_Extender #(.in_width(32), .out_width(11)) bit_extender_1 (.in(Rs_Imm), .out(bit_extender_1_out));
  memory dmem (.A(bit_extender_1_out), .Clock(Clock), .Load(not_1_out), .Data(dmem_data));  // open: en, Clear
  not not_1 (not_1_out, Lw);
  assign dmem_data = Sw ? SwRt : 32'bz;  // Controlled_Buffer controlled_buffer_1
  assign controlled_buffer_2_out = Lw ? dmem_data : 32'bz;  // Controlled_Buffer controlled_buffer_2
  Multiplexer #(.width(32), .enable("false")) multiplexer_1 (
    .in0(Rs_Imm), .in1(controlled_buffer_2_out), .out(Out), .sel(Lw));
endmodule

module WB (
  input  [31:0] LW_Out,
  input  [31:0] WrRegData,
  input  [8:0] Opcode,
  input  WrSig
);

  wire and_1_out;

  and and_1 (and_1_out, ~Opcode[8], ~Opcode[3]);  // AND_Gate
  or or_1 (WrSig, Opcode[8], and_1_out);

  assign WrRegData = LW_Out;
endmodule

module DPRF (
  input  [3:0] WrDest,
  input  Clock,
  input  [3:0] RdSrc1,
  input  [31:0] WrData,
  input  [3:0] RdSrc2,
  input  WrEn,
  output [31:0] RdData1,
  output [31:0] RdData2
);

  wire Wr1, Wr2, Wr3, Wr4, Wr5, Wr6, Wr7, Wr8, Wr9, Wr10, Wr11, Wr12, Wr13, Wr14, Wr15;
  wire [31:0] Rd1, Rd2, Rd3, Rd4, Rd5, Rd6, Rd7, Rd8, Rd9, Rd10, Rd11, Rd12, Rd13, Rd14, Rd15;

  Demultiplexer #(.select(4), .enable("false")) demultiplexer_1 (
    .out1(Wr1), .out2(Wr2), .out3(Wr3), .out4(Wr4), .out5(Wr5), .out6(Wr6), .out7(Wr7), .out8(Wr8),
    .out9(Wr9), .out10(Wr10), .out11(Wr11), .out12(Wr12), .out13(Wr13), .out14(Wr14), .out15(Wr15),
    .in(WrEn), .sel(WrDest));  // open: out0
  Register #(.width(32)) a3__rv (.D(WrData), .en(Wr4), .Q(Rd4), .clk(Clock));  // open: clr
  Register #(.width(32)) s1 (.D(WrData), .en(Wr8), .Q(Rd8), .clk(Clock));  // open: clr
  Register #(.width(32)) r12 (.D(WrData), .en(Wr12), .Q(Rd12), .clk(Clock));  // open: clr
  Register #(.width(32)) a0 (.D(WrData), .en(Wr1), .Q(Rd1), .clk(Clock));  // open: clr
  Register #(.width(32)) t0 (.D(WrData), .en(Wr5), .Q(Rd5), .clk(Clock));  // open: clr
  Register #(.width(32)) s2 (.D(WrData), .en(Wr9), .Q(Rd9), .clk(Clock));  // open: clr
  Register #(.width(32)) FP (.D(WrData), .en(Wr13), .Q(Rd13), .clk(Clock));  // open: clr
  Register #(.width(32)) SP (.D(WrData), .en(Wr14), .Q(Rd14), .clk(Clock));  // open: clr
  Register #(.width(32)) a1 (.D(WrData), .en(Wr2), .Q(Rd2), .clk(Clock));  // open: clr
  Register #(.width(32)) t1 (.D(WrData), .en(Wr6), .Q(Rd6), .clk(Clock));  // open: clr
  Register #(.width(32)) r10 (.D(WrData), .en(Wr10), .Q(Rd10), .clk(Clock));  // open: clr
  Register #(.width(32)) a2 (.D(WrData), .en(Wr3), .Q(Rd3), .clk(Clock));  // open: clr
  Register #(.width(32)) s0 (.D(WrData), .en(Wr7), .Q(Rd7), .clk(Clock));  // open: clr
  Register #(.width(32)) r11 (.D(WrData), .en(Wr11), .Q(Rd11), .clk(Clock));  // open: clr
  Register #(.width(32)) RA (.D(WrData), .en(Wr15), .Q(Rd15), .clk(Clock));  // open: clr
  Multiplexer #(.select(4), .width(32), .enable("false")) multiplexer_1 (
    .in0({32{1'b0}}), .in1(Rd1), .in2(Rd2), .in3(Rd3), .in4(Rd4), .in5(Rd5), .in6(Rd6), .in7(Rd7), .in8(Rd8),
    .in9(Rd9), .in10(Rd10), .in11(Rd11), .in12(Rd12), .in13(Rd13), .in14(Rd14), .in15(Rd15), .out(RdData1),
    .sel(RdSrc1));
  Multiplexer #(.select(4), .width(32), .enable("false")) multiplexer_2 (
    .in0({32{1'b0}}), .in1(Rd1), .in2(Rd2), .in3(Rd3), .in4(Rd4), .in5(Rd5), .in6(Rd6), .in7(Rd7), .in8(Rd8),
    .in9(Rd9), .in10(Rd10), .in11(Rd11), .in12(Rd12), .in13(Rd13), .in14(Rd14), .in15(Rd15), .out(RdData2),
    .sel(RdSrc2));

  // Other names for the same wires on the sheet: Data1[31:0] = RdData1; Data2[31:0] = RdData2; Dest[3:0] = WrDest;
  //   Src1[3:0] = RdSrc1; Src2[3:0] = RdSrc2
endmodule

module ALU (
  input  [31:0] A,
  input  [31:0] B,
  input  [2:0] Func,
  output [31:0] Out
);

  wire [31:0] adder_1_out;

  Adder #(.width(32)) adder_1 (.a(A), .b(B), .out(adder_1_out));  // open: cin, cout
  Multiplexer #(.select(3), .width(32), .enable("false")) multiplexer_1 (
    .in0(adder_1_out), .out(Out), .sel(Func));  // open: in1, in2, in3, in4, in5, in6, in7

  // Notes on the sheet:
  //   Rest (and, or, xor, sub, nand, nor,nxor) to be implemented in verilog
endmodule

module SignalGen (
  input  [8:0] Opcode,
  output Eq,
  output Lt,
  output Le,
  output Neq,
  output Add,
  output And,
  output Or,
  output Xor,
  output Sub,
  output Nand,
  output Nor,
  output Nxor,
  output Rshf,
  output Lshf,
  output Beq,
  output Blt,
  output Ble,
  output Bneq,
  output Jal,
  output Lw,
  output Sw,
  output Addi,
  output Andi,
  output Ori,
  output Xori
);

  Comparator #(.width(7)) comparator_1 (.a({Opcode[8], Opcode[5:0]}), .b(7'b1001000), .eq(Eq));  // open: gt, lt
  Comparator #(.width(7)) comparator_2 (.a({Opcode[8], Opcode[5:0]}), .b(7'b1001001), .eq(Lt));  // open: gt, lt
  Comparator #(.width(7)) comparator_3 (.a({Opcode[8], Opcode[5:0]}), .b(7'b1001010), .eq(Le));  // open: gt, lt
  Comparator #(.width(7)) comparator_4 (.a({Opcode[8], Opcode[5:0]}), .b(7'b1001011), .eq(Neq));  // open: gt, lt
  Comparator #(.width(7)) comparator_5 (.a({Opcode[8], Opcode[5:0]}), .b(7'b1100000), .eq(Add));  // open: gt, lt
  Comparator #(.width(7)) comparator_6 (.a({Opcode[8], Opcode[5:0]}), .b(7'b1100100), .eq(And));  // open: gt, lt
  Comparator #(.width(7)) comparator_7 (.a({Opcode[8], Opcode[5:0]}), .b(7'b1100101), .eq(Or));  // open: gt, lt
  Comparator #(.width(7)) comparator_8 (.a({Opcode[8], Opcode[5:0]}), .b(7'b1100110), .eq(Xor));  // open: gt, lt
  Comparator #(.width(7)) comparator_9 (.a({Opcode[8], Opcode[5:0]}), .b(7'b1101000), .eq(Sub));  // open: gt, lt
  Comparator #(.width(7)) comparator_10 (.a({Opcode[8], Opcode[5:0]}), .b(7'b1101100), .eq(Nand));  // open: gt, lt
  Comparator #(.width(7)) comparator_11 (.a({Opcode[8], Opcode[5:0]}), .b(7'b1101101), .eq(Nor));  // open: gt, lt
  Comparator #(.width(7)) comparator_12 (.a({Opcode[8], Opcode[5:0]}), .b(7'b1101110), .eq(Nxor));  // open: gt, lt
  Comparator #(.width(7)) comparator_13 (.a({Opcode[8], Opcode[5:0]}), .b(7'b1110000), .eq(Rshf));  // open: gt, lt
  Comparator #(.width(7)) comparator_14 (.a({Opcode[8], Opcode[5:0]}), .b(7'b1110001), .eq(Lshf));  // open: gt, lt
  Comparator #(.width(7)) comparator_15 (.a({Opcode[8], Opcode[5:0]}), .b(7'b0001000), .eq(Beq));  // open: gt, lt
  Comparator #(.width(7)) comparator_16 (.a({Opcode[8], Opcode[5:0]}), .b(7'b0001001), .eq(Blt));  // open: gt, lt
  Comparator #(.width(7)) comparator_17 (.a({Opcode[8], Opcode[5:0]}), .b(7'b0001010), .eq(Ble));  // open: gt, lt
  Comparator #(.width(7)) comparator_18 (.a({Opcode[8], Opcode[5:0]}), .b(7'b0001011), .eq(Bneq));  // open: gt, lt
  Comparator #(.width(7)) comparator_19 (.a({Opcode[8], Opcode[5:0]}), .b(7'b0001100), .eq(Jal));  // open: gt, lt
  Comparator #(.width(7)) comparator_20 (.a({Opcode[8], Opcode[5:0]}), .b(7'b0010010), .eq(Lw));  // open: gt, lt
  Comparator #(.width(7)) comparator_21 (.a({Opcode[8], Opcode[5:0]}), .b(7'b0011010), .eq(Sw));  // open: gt, lt
  Comparator #(.width(7)) comparator_22 (.a({Opcode[8], Opcode[5:0]}), .b(7'b0100000), .eq(Addi));  // open: gt, lt
  Comparator #(.width(7)) comparator_23 (.a({Opcode[8], Opcode[5:0]}), .b(7'b0100100), .eq(Andi));  // open: gt, lt
  Comparator #(.width(7)) comparator_24 (.a({Opcode[8], Opcode[5:0]}), .b(7'b0100101), .eq(Ori));  // open: gt, lt
  Comparator #(.width(7)) comparator_25 (.a({Opcode[8], Opcode[5:0]}), .b(7'b0100110), .eq(Xori));  // open: gt, lt

  // Other names for the same wires on the sheet: Op[6:0] = {Opcode[8], Opcode[5:0]}
endmodule
